# Fritzing sketch diagram (saved by Fritzing 0.9.3b)

parts:
  Part1 = Arduino Mega 2560 (Rev3)
  M1 = fc-51 [package=THT]
  S1 = H-Bridge with L298N
  M2 = Stepper Motor - Bipolar
  VCC1 = Battery block 9V

nets:
  N1: Part1.D11_PWM, S1.IN4
  N2: Part1.D10_PWM, S1.IN3
  N3: Part1.D9_PWM, S1.IN2
  N4: Part1.D8_PWM, S1.IN1
  N5: Part1.5V, M1.pin3
  GND: Part1.GND, M1.pin2, S1.GND, VCC1.-
  VIN: Part1.VIN, S1.5V
  N6: Part1.D5_PWM, M1.pin1
  N7: S1.12V, VCC1.+
  N8: S1.M1-01, M2.C
  N9: S1.M1-02, M2.A
  N10: S1.M2-01, M2.B
  N11: S1.M2-02, M2.D

custom parts:
  H-Bridge with L298N: h-bridge
